# Fritzing sketch serverPiControl (saved by Fritzing 0.9.1b)
breadboards: 1

parts:
  Raspberry_Pi1 = Raspberry Pi B rev2
  LED1 = smd LED [color="Green (555nm)" package="0603 [SMD]"]
  LED2 = smd LED [color="Blue (430nm)" package="0603 [SMD]"]
  LED3 = smd LED [color="Red (633nm)" package="0603 [SMD]"]
  LED4 = smd LED [color="White (6500K)" package="0603 [SMD]"]
  R4 = Resistor [tolerance=±5% resistance=1k package="0603 [SMD]"]
  R1 = Resistor [tolerance=±5% resistance=1k package="0603 [SMD]"]
  R2 = Resistor [tolerance=±5% resistance=1k package="0603 [SMD]"]
  R3 = Resistor [tolerance=±5% resistance=1k package="0603 [SMD]"]

nets:
  N1: Raspberry_Pi1.GND, LED1.cathode, LED2.cathode, LED3.cathode, LED4.cathode
  N2: Raspberry_Pi1.GPIO_14, R4.Pin_0
  N3: Raspberry_Pi1.GPIO_15, R3.Pin_0
  N4: Raspberry_Pi1.GPIO_18, R2.Pin_0
  N5: Raspberry_Pi1.GPIO_25, R1.Pin_0
  N6: LED1.anode, R4.Pin_1
  N7: LED2.anode, R3.Pin_1
  N8: LED3.anode, R2.Pin_1
  N9: LED4.anode, R1.Pin_1
